// Logisim project Half adder.circ as structural Verilog
module main (
  input  in_1,
  input  in_2,
  output out_3
);

  wire and_1_out, not_1_out, or_1_out;

  not not_1 (not_1_out, in_1);
  or or_1 (or_1_out, in_1, in_1, in_2, in_2);
  and and_1 (and_1_out, not_1_out, or_1_out);
  or or_2 (out_3, and_1_out, or_1_out);
endmodule

module _2 (
  input  in_1,
  input  in_2,
  input  in_3,
  output out_4
);

  wire and_1_out, and_2_out, not_1_out, not_2_out, or_1_out;

  and and_1 (and_1_out, in_1, in_2, in_3);
  not not_1 (not_1_out, in_2);
  not not_2 (not_2_out, in_3);
  or or_1 (or_1_out, not_1_out, not_2_out);
  and and_2 (and_2_out, in_1, or_1_out);
  or or_2 (out_4, and_1_out, and_2_out);
endmodule

module _3 (
  input  in_1,
  input  in_2,
  input  in_3,
  input  in_4,
  output out_5
);

  wire and_1_out, buffer_1_out, not_1_out, or_1_out, xor_1_out, xor_2_out;

  not not_1 (not_1_out, in_4);
  and and_1 (and_1_out, in_1, not_1_out);
  or or_1 (or_1_out, in_3, xor_1_out);
  xor xor_1 (xor_1_out, in_1, in_4);
  xor xor_2 (xor_2_out, and_1_out, in_2);
  buf buffer_1 (buffer_1_out, or_1_out);
  or or_2 (out_5, xor_2_out, buffer_1_out);
endmodule

module problem_2 (
  input  in_1,
  input  in_2,
  output out_3
);

  wire and_1_out, and_2_out, not_1_out, not_2_out;

  not not_1 (not_1_out, in_1);
  not not_2 (not_2_out, in_2);
  and and_1 (and_1_out, in_2, not_1_out);
  and and_2 (and_2_out, not_2_out, in_1);
  or or_1 (out_3, and_1_out, and_2_out);
endmodule

module prob_3 (
  input  in_1,
  input  in_2,
  input  in_3,
  output out_4
);

  wire nand_1_out, not_1_out;

  nand nand_1 (nand_1_out, in_1, in_1, in_2);
  not not_1 (not_1_out, in_3);
  and and_1 (out_4, nand_1_out, in_2, not_1_out);
endmodule

module k (
  input  in_1,
  input  in_2,
  input  in_3,
  output out_4,
  output out_5
);

  wire and_1_out, and_2_out, and_3_out;

  ExactlyOne xor_1 (.out(out_4), .in0(in_1), .in2(in_2), .in4(in_3));
  and and_1 (and_1_out, in_3, in_1);
  and and_2 (and_2_out, in_1, in_2);
  and and_3 (and_3_out, in_3, in_2);
  or or_1 (out_5, and_1_out, and_2_out, and_3_out, and_3_out, and_3_out);
endmodule

module problem_6 (
  input  in_1,
  input  in_2,
  input  in_3,
  output out_4
);

  wire and_1_out, and_2_out, and_3_out;

  and and_1 (and_1_out, in_1, in_2);
  and and_2 (and_2_out, in_1, in_1, in_3);
  and and_3 (and_3_out, in_1, in_3, in_2);
  or or_1 (out_4, and_1_out, and_2_out, and_3_out);
endmodule

module _7 (
  input  in_1,
  input  in_2,
  input  in_3,
  output out_4
);

  wire nand_1_out, nand_2_out, not_1_out;

  not not_1 (not_1_out, in_1);
  nand nand_1 (nand_1_out, in_1, in_1, in_2);
  nand nand_2 (nand_2_out, not_1_out, in_3);
  nand nand_3 (out_4, nand_1_out, nand_2_out);
endmodule

module exp_2 (
  input  in_1,
  input  in_2,
  output out_3
);

  wire and_1_out, and_2_out, not_1_out;

  not not_1 (not_1_out, in_1);
  and and_1 (and_1_out, not_1_out, in_2);
  and and_2 (and_2_out, in_1, in_2);
  or or_1 (out_3, and_1_out, and_2_out);
endmodule

module exp_2_2nd_question (
  input  in_1,
  input  in_2,
  input  in_3,
  output out_4
);

  wire and_1_out, and_2_out, and_3_out, and_4_out, not_1_out, not_2_out, not_3_out;

  not not_1 (not_1_out, in_1);
  not not_2 (not_2_out, in_2);
  not not_3 (not_3_out, in_3);
  and and_1 (and_1_out, in_2, not_1_out, in_3);
  and and_2 (and_2_out, in_2, in_1, not_3_out);
  and and_3 (and_3_out, not_1_out, not_2_out, not_3_out);
  and and_4 (and_4_out, in_1, in_2, in_3);
  or or_1 (out_4, and_1_out, and_2_out, and_3_out, and_4_out);
endmodule

module a_b__c_d (
  input  in_1,
  input  in_2,
  input  in_3,
  input  in_4,
  output out_5
);

  wire or_1_out, or_2_out;

  or or_1 (or_1_out, in_1, in_2);
  or or_2 (or_2_out, in_3, in_4);
  and and_1 (out_5, or_1_out, or_2_out);
endmodule

module Half_adder (
  input  in_1,
  input  in_2,
  output out_3,
  output out_4
);

  xor xor_1 (out_3, in_1, in_2);
  and and_1 (out_4, in_1, in_2);
endmodule

module Full_adder (
  input  in_1,
  input  in_2,
  input  in_3,
  output SUM,
  output CARRY
);

  wire and_1_out, and_2_out, xor_1_out;

  xor xor_1 (xor_1_out, in_1, in_2);
  xor xor_2 (SUM, xor_1_out, in_3);
  and and_1 (and_1_out, xor_1_out, in_3);
  and and_2 (and_2_out, in_1, in_2);
  or or_1 (CARRY, and_1_out, and_2_out);
endmodule
