// Logisim project parity checker circuit.circ as structural Verilog
module main (
  input  in_1,
  input  in_2,
  output out_3
);

  wire and_1_out, not_1_out, or_1_out;

  not not_1 (not_1_out, in_1);
  or or_1 (or_1_out, in_1, in_1, in_2, in_2);
  and and_1 (and_1_out, not_1_out, or_1_out);
  or or_2 (out_3, and_1_out, or_1_out);
endmodule

module _2 (
  input  in_1,
  input  in_2,
  input  in_3,
  output out_4
);

  wire and_1_out, and_2_out, not_1_out, not_2_out, or_1_out;

  and and_1 (and_1_out, in_1, in_2, in_3);
  not not_1 (not_1_out, in_2);
  not not_2 (not_2_out, in_3);
  or or_1 (or_1_out, not_1_out, not_2_out);
  and and_2 (and_2_out, in_1, or_1_out);
  or or_2 (out_4, and_1_out, and_2_out);
endmodule

module _3 (
  input  in_1,
  input  in_2,
  input  in_3,
  input  in_4,
  output out_5
);

  wire and_1_out, buffer_1_out, not_1_out, or_1_out, xor_1_out, xor_2_out;

  not not_1 (not_1_out, in_4);
  and and_1 (and_1_out, in_1, not_1_out);
  or or_1 (or_1_out, in_3, xor_1_out);
  xor xor_1 (xor_1_out, in_1, in_4);
  xor xor_2 (xor_2_out, and_1_out, in_2);
  buf buffer_1 (buffer_1_out, or_1_out);
  or or_2 (out_5, xor_2_out, buffer_1_out);
endmodule

module problem_2 (
  input  in_1,
  input  in_2,
  output out_3
);

  wire and_1_out, and_2_out, not_1_out, not_2_out;

  not not_1 (not_1_out, in_1);
  not not_2 (not_2_out, in_2);
  and and_1 (and_1_out, in_2, not_1_out);
  and and_2 (and_2_out, not_2_out, in_1);
  or or_1 (out_3, and_1_out, and_2_out);
endmodule

module prob_3 (
  input  in_1,
  input  in_2,
  input  in_3,
  output out_4
);

  wire nand_1_out, not_1_out;

  nand nand_1 (nand_1_out, in_1, in_1, in_2);
  not not_1 (not_1_out, in_3);
  and and_1 (out_4, nand_1_out, in_2, not_1_out);
endmodule

module k (
  input  in_1,
  input  in_2,
  input  in_3,
  output out_4,
  output out_5
);

  wire and_1_out, and_2_out, and_3_out;

  ExactlyOne xor_1 (.out(out_4), .in0(in_1), .in2(in_2), .in4(in_3));
  and and_1 (and_1_out, in_3, in_1);
  and and_2 (and_2_out, in_1, in_2);
  and and_3 (and_3_out, in_3, in_2);
  or or_1 (out_5, and_1_out, and_2_out, and_3_out, and_3_out, and_3_out);
endmodule

module problem_6 (
  input  in_1,
  input  in_2,
  input  in_3,
  output out_4
);

  wire and_1_out, and_2_out, and_3_out;

  and and_1 (and_1_out, in_1, in_2);
  and and_2 (and_2_out, in_1, in_1, in_3);
  and and_3 (and_3_out, in_1, in_3, in_2);
  or or_1 (out_4, and_1_out, and_2_out, and_3_out);
endmodule

module _7 (
  input  in_1,
  input  in_2,
  input  in_3,
  output out_4
);

  wire nand_1_out, nand_2_out, not_1_out;

  not not_1 (not_1_out, in_1);
  nand nand_1 (nand_1_out, in_1, in_1, in_2);
  nand nand_2 (nand_2_out, not_1_out, in_3);
  nand nand_3 (out_4, nand_1_out, nand_2_out);
endmodule

module exp_2 (
  input  in_1,
  input  in_2,
  output out_3
);

  wire and_1_out, and_2_out, not_1_out;

  not not_1 (not_1_out, in_1);
  and and_1 (and_1_out, not_1_out, in_2);
  and and_2 (and_2_out, in_1, in_2);
  or or_1 (out_3, and_1_out, and_2_out);
endmodule

module exp_2_2nd_question (
  input  in_1,
  input  in_2,
  input  in_3,
  output out_4
);

  wire and_1_out, and_2_out, and_3_out, and_4_out, not_1_out, not_2_out, not_3_out;

  not not_1 (not_1_out, in_1);
  not not_2 (not_2_out, in_2);
  not not_3 (not_3_out, in_3);
  and and_1 (and_1_out, in_2, not_1_out, in_3);
  and and_2 (and_2_out, in_2, in_1, not_3_out);
  and and_3 (and_3_out, not_1_out, not_2_out, not_3_out);
  and and_4 (and_4_out, in_1, in_2, in_3);
  or or_1 (out_4, and_1_out, and_2_out, and_3_out, and_4_out);
endmodule

module a_b__c_d (
  input  in_1,
  input  in_2,
  input  in_3,
  input  in_4,
  output out_5
);

  wire or_1_out, or_2_out;

  or or_1 (or_1_out, in_1, in_2);
  or or_2 (or_2_out, in_3, in_4);
  and and_1 (out_5, or_1_out, or_2_out);
endmodule

module Half_adder (
  input  in_1,
  input  in_2,
  output out_3
);

  wire and_1_out;

  xor xor_1 (out_3, in_1, in_2);
  and and_1 (and_1_out, in_1, in_2);
endmodule

module Full_adder (
  input  in_1,
  input  in_2,
  input  in_3,
  output out_4,
  output out_5
);

  wire and_1_out, and_2_out, xor_1_out;

  xor xor_1 (xor_1_out, in_1, in_2);
  xor xor_2 (out_4, xor_1_out, in_3);
  and and_1 (and_1_out, xor_1_out, in_3);
  and and_2 (and_2_out, in_1, in_2);
  or or_1 (out_5, and_1_out, and_2_out);
endmodule

module logisim_digrams_mod_2 (
  input  in_1,
  input  in_2,
  input  in_3,
  output out_4,
  output out_5
);

  wire and_1_out, and_2_out, and_3_out, xor_1_out;

  xor xor_1 (xor_1_out, in_1, in_2);
  and and_1 (and_1_out, in_1, in_2);
  and and_2 (and_2_out, in_2, in_3);
  and and_3 (and_3_out, in_3, in_1);
  xor xor_2 (out_4, xor_1_out, in_3);
  or or_1 (out_5, and_1_out, and_2_out, and_3_out);
endmodule

module mod_2_ripple_carry (
  input  in_1,
  input  in_2,
  input  in_3,
  input  in_4,
  input  in_5,
  input  in_6,
  input  in_7,
  input  in_8,
  input  in_9,
  output out_10,
  output out_11,
  output out_12,
  output out_13,
  output out_14
);

  wire adder_1_cout, adder_2_cout, adder_3_cout, adder_4_cout, adder_4_out;

  Adder #(.width(1)) adder_1 (.a(in_2), .b(in_3), .out(out_10), .cin(in_1), .cout(adder_1_cout));
  Adder #(.width(1)) adder_2 (.a(in_4), .b(in_5), .out(out_11), .cin(adder_1_cout), .cout(adder_2_cout));
  Adder #(.width(1)) adder_3 (.a(in_6), .b(in_7), .out(out_12), .cin(adder_2_cout), .cout(adder_3_cout));
  Adder #(.width(1)) adder_4 (.a(in_8), .b(in_9), .out(adder_4_out), .cin(adder_3_cout), .cout(adder_4_cout));
endmodule

module serial_in_parr_allel_out_and_parallel_in_serial_out (
  input  in_1,
  input  in_2,
  input  in_3,
  output out_4,
  output out_5,
  output out_6,
  output out_7
);

  wire clock_1_out;

  Clock clock_1 (.out(clock_1_out));
  D_Flip_Flop d_ff_1 (.clk(clock_1_out), .D(in_1), .Q(out_4), .preset(in_2), .reset(in_3));  // open: Qn, en
  D_Flip_Flop d_ff_2 (.clk(clock_1_out), .D(out_4), .Q(out_5), .preset(in_2), .reset(in_3));  // open: Qn, en
  D_Flip_Flop d_ff_3 (.clk(clock_1_out), .D(out_5), .Q(out_6), .preset(in_2), .reset(in_3));  // open: Qn, en
  D_Flip_Flop d_ff_4 (.clk(clock_1_out), .D(out_6), .Q(out_7), .preset(in_2), .reset(in_3));  // open: Qn, en
endmodule

module project_2 (
  input  in_1,
  input  in_2,
  input  in_3,
  input  in_4,
  output out_5
);

  wire XOR_2_out, XOR_out;

  xor XOR (XOR_out, in_1, in_2);
  xor XOR_2 (XOR_2_out, in_3, in_4);
  xor XOR_3 (out_5, XOR_out, XOR_2_out);
endmodule

module parity_generator_circuit (
  input  in_1,
  input  in_2,
  input  in_3,
  input  in_4,
  output out_5
);

  wire XOR_2_out, XOR_out;

  xor XOR (XOR_out, in_1, in_2);
  xor XOR_2 (XOR_2_out, in_3, in_4);
  xor XOR_3 (out_5, XOR_out, XOR_2_out);
endmodule

module parity_checker_circuit (
  input  in_1,
  input  in_2,
  input  in_3,
  input  in_4,
  input  in_5,
  output out_6
);

  wire XOR_2_out, XOR_3_out, XOR_out;

  xor XOR (XOR_out, in_1, in_2);
  xor XOR_2 (XOR_2_out, in_3, in_4);
  xor XOR_3 (XOR_3_out, XOR_out, XOR_2_out);
  xor XOR_4 (out_6, XOR_3_out, in_5);
endmodule
